# Fritzing sketch repeat (saved by Fritzing 0.9.1b)
breadboards: 2

parts:
  S1 = Pushbutton [package="[THT]"]
  S2 = Pushbutton [package="[THT]"]
  S3 = Pushbutton [package="[THT]"]
  S4 = Pushbutton [package="[THT]"]
  LED1 = LED - 5mm [color="Red (633nm)" package="5 mm [THT]"]
  LED2 = LED - 5mm [color="Yellow (574nm)" package="5 mm [THT]"]
  LED3 = LED - 5mm [color="Green (555nm)" package="5 mm [THT]"]
  LED4 = LED - 5mm [color="Blue (430nm)" package="5 mm [THT]"]
  R1 = Resistor [tolerance=±5% resistance=220 package=THT]
  R2 = Resistor [tolerance=±5% resistance=220 package=THT]
  R3 = Resistor [tolerance=±5% resistance=220 package=THT]
  R4 = Resistor [tolerance=±5% resistance=220 package=THT]
  part = Resistor [tolerance=±5% resistance=220 package=THT]  # not connected
  Pi1 = Adafruit Pi Cobbler

nets:
  GND: S1.Pin_1, S1.Pin_2, S2.Pin_1, S2.Pin_2, S3.Pin_1, S3.Pin_2, S4.Pin_1, S4.Pin_2, LED1.cathode, LED2.cathode, LED3.cathode, LED4.cathode, Pi1.GND
  button1: S1.Pin_3, S1.Pin_4, Pi1.#4
  button2: S2.Pin_3, S2.Pin_4, Pi1.#18
  button3: S3.Pin_3, S3.Pin_4, Pi1.#23
  button4: S4.Pin_3, S4.Pin_4, Pi1.#17
  N1: LED1.anode, R1.Pin_1
  N2: LED2.anode, R2.Pin_0
  N3: LED3.anode, R3.Pin_0
  N4: LED4.anode, R4.Pin_1
  light1: R1.Pin_0, Pi1.#21
  light2: R2.Pin_1, Pi1.#24
  light3: R3.Pin_1, Pi1.#25
  light4: R4.Pin_0, Pi1.#22

notes:
  Choose R1-R4 based on the desired LEDs and drive current (based on the roughly 3.3V high output). 220Ω is a good starting point, but higher-voltage LEDs may require a lower value.
  Note that the program enables the GPIO's own built-in pull-up resistors, so no pull-ups need to be added here.
  The program uses the Pi's audio output, so no speaker appears in this schematic. Make sure to plug in a speaker or headphones in order to hear the tones.
  The revision of Pi used by the program calls the light1 pin 27 rather than 21. Adjust the code if necessary.

custom parts:
  Adafruit Pi Cobbler: Adafruit Pi Cobbler GPIO Breakout for Raspberry Pi
